// Logisim project 1.circ as structural Verilog: 1 circuit, main circuit main
module main (
  input  in_1,
  input  in_2,
  input  in_3,
  input  in_4
);

  wire button_1_out, button_2_out, button_3_out, rgbled_1_p4;
  wire [7:0] adder_1_out, adder_2_out, d_ff_8_q, multiplexer_1_out, ram_1_dout, register_1_q;

  // RGBLED rgbled_1: pin names not known; wires that end beside it: in_3, in_2, in_4, rgbled_1_p4, rgbled_1_p4, d_ff_8_q[7]
  Button button_1 (.out(button_1_out));
  Button button_2 (.out(button_2_out));
  LED led_1 (.in(button_2_out));
  // Probe on ram_1_dout
  D_Flip_Flop d_ff_1 (.D(in_1), .clk(button_1_out), .Q(d_ff_8_q[7]));  // open: Qn, preset, reset
  Adder adder_1 (.a(register_1_q), .b(8'h1), .out(adder_1_out));  // open: cin, cout
  Adder adder_2 (.a({8{1'b1}}), .b(register_1_q), .out(adder_2_out));  // open: cin, cout
  // Probe on d_ff_8_q[7]
  D_Flip_Flop d_ff_2 (.D(d_ff_8_q[7]), .clk(button_1_out), .Q(d_ff_8_q[6]));  // open: Qn, preset, reset
  Register register_1 (.D(multiplexer_1_out), .clk(button_3_out), .Q(register_1_q));  // open: en, clr
  Multiplexer #(.enable("false"), .width(8)) multiplexer_1 (
    .in0(adder_1_out), .in1(adder_2_out), .out(multiplexer_1_out), .sel(ram_1_dout[0]));
  Button button_3 (.out(button_3_out));
  // Probe on d_ff_8_q[6]
  D_Flip_Flop d_ff_3 (.D(d_ff_8_q[6]), .clk(button_1_out), .Q(d_ff_8_q[5]));  // open: Qn, preset, reset
  // Probe on d_ff_8_q[5]
  // Probe on d_ff_8_q[4]
  D_Flip_Flop d_ff_4 (.D(d_ff_8_q[5]), .clk(button_1_out), .Q(d_ff_8_q[4]));  // open: Qn, preset, reset
  D_Flip_Flop d_ff_5 (.D(d_ff_8_q[4]), .clk(button_1_out), .Q(d_ff_8_q[3]));  // open: Qn, preset, reset
  D_Flip_Flop d_ff_6 (.D(d_ff_8_q[3]), .clk(button_1_out), .Q(d_ff_8_q[2]));  // open: Qn, preset, reset
  RAM #(.asyncread("true")) ram_1 (.addr(register_1_q), .dout(ram_1_dout));  // open: we, oe, clk, din
  D_Flip_Flop d_ff_7 (.D(d_ff_8_q[2]), .clk(button_1_out), .Q(d_ff_8_q[1]));  // open: Qn, preset, reset
  D_Flip_Flop d_ff_8 (.D(d_ff_8_q[1]), .clk(button_1_out), .Q(d_ff_8_q[0]));  // open: Qn, preset, reset
endmodule
