// Logisim project work1.circ as structural Verilog
module mian (
  input  try1,
  output try2
);

  buf buffer_1 (try2, try1);
endmodule

module mux121 (
  input  a,
  input  b,
  input  s,
  output c
);

  wire and_1_out, and_2_out, not_1_out;

  not not_1 (not_1_out, s);
  and and_1 (and_1_out, not_1_out, a);
  and and_2 (and_2_out, b, s);
  or or_1 (c, and_1_out, and_2_out);
  // Probe on c
endmodule

module add11 (
  input  a,
  input  b,
  input  c,
  output p1,
  output sigma,
  output c1,
  output g1
);

  wire and_1_out;

  xor xor_1 (p1, a, b);
  // Probe on p1
  xor xor_2 (sigma, p1, c);
  and and_1 (and_1_out, p1, c);
  and and_2 (g1, a, b);
  // Probe on g1
  or or_1 (c1, and_1_out, g1);
  // Probe on c1
  // Probe on sigma
endmodule

module add41 (
  input  in_1,
  input  [3:0] in_2,
  input  [3:0] in_3,
  output c4,
  output p1,
  output g1,
  output [3:0] sigma
);

  wire add11_1_g1, add11_1_p1, add11_2_g1, add11_2_p1, add11_3_g1, add11_3_p1, add11_4_g1, add11_4_p1,
       adder_1_cout, and_1_out, and_2_out, and_3_out, and_4_out, and_5_out, and_6_out, and_7_out, and_8_out,
       and_9_out, and_10_out, and_11_out, button_1_out, button_2_out, comparator_1_eq, comparator_2_eq,
       for441_1_f8, not_1_out;
  wire [3:0] add11_4_c1, adder_1_out, for441_1_f0, for441_1_f4, multiplexer_1_out, multiplexer_2_out;
  wire [3:1] or_4_out;

  Multiplexer #(.enable("false"), .width(4)) multiplexer_1 (
    .in0(in_2), .in1(for441_1_f4), .out(multiplexer_1_out), .sel(1'b0));
  Multiplexer #(.enable("false"), .width(4)) multiplexer_2 (
    .in0(in_3), .in1(for441_1_f0), .out(multiplexer_2_out), .sel(1'b0));
  // Probe on multiplexer_1_out
  Adder #(.width(4)) adder_1 (
    .a(multiplexer_1_out), .b(multiplexer_2_out), .out(adder_1_out), .cin(add11_4_c1[0]), .cout(adder_1_cout));
  // Probe on multiplexer_2_out
  // Probe on {c4, add11_4_c1}
  // Probe on {g1, or_4_out, add11_4_c1[0]}
  // Probe on adder_1_out
  // Probe on sigma
  // Probe on adder_1_cout
  // Probe on c4
  Comparator #(.width(4)) comparator_1 (.a(sigma), .b(adder_1_out), .eq(comparator_1_eq));  // open: gt, lt
  add11 add11_1 (
    .a(multiplexer_2_out[3]), .b(multiplexer_1_out[3]), .c(or_4_out[3]), .p1(add11_1_p1), .sigma(sigma[3]),
    .c1(c4), .g1(add11_1_g1));
  add11 add11_2 (
    .a(multiplexer_2_out[2]), .b(multiplexer_1_out[2]), .c(or_4_out[2]), .p1(add11_2_p1), .sigma(sigma[2]),
    .c1(add11_4_c1[3]), .g1(add11_2_g1));
  add11 add11_3 (
    .a(multiplexer_2_out[1]), .b(multiplexer_1_out[1]), .c(or_4_out[1]), .p1(add11_3_p1), .sigma(sigma[1]),
    .c1(add11_4_c1[2]), .g1(add11_3_g1));
  add11 add11_4 (
    .a(multiplexer_2_out[0]), .b(multiplexer_1_out[0]), .c(add11_4_c1[0]), .p1(add11_4_p1), .sigma(sigma[0]),
    .c1(add11_4_c1[1]), .g1(add11_4_g1));
  Comparator #(.width(5)) comparator_2 (
    .a({c4, add11_4_c1}), .b({g1, or_4_out, add11_4_c1[0]}), .eq(comparator_2_eq));  // open: gt, lt
  Multiplexer #(.enable("false")) multiplexer_3 (.in0(in_1), .in1(for441_1_f8), .out(add11_4_c1[0]), .sel(1'b0));
  for441 for441_1 (.re(button_1_out), .add1(button_2_out), .f0(for441_1_f0), .f4(for441_1_f4), .f8(for441_1_f8));
  and and_1 (and_1_out, comparator_2_eq, comparator_1_eq);
  LED led_1 (.in(and_1_out));
  not not_1 (not_1_out, and_1_out);
  LED led_2 (.in(not_1_out));
  Button button_1 (.out(button_1_out));
  and and_2 (and_2_out, add11_1_p1, add11_2_g1);
  and and_3 (and_3_out, add11_1_p1, add11_2_p1, add11_3_g1);
  and and_4 (and_4_out, add11_1_p1, add11_2_p1, add11_3_p1, add11_4_g1);
  and and_5 (and_5_out, add11_1_p1, add11_2_p1, add11_3_p1, add11_4_p1, add11_4_c1[0]);
  and and_6 (and_6_out, add11_2_p1, add11_3_g1);
  and and_7 (and_7_out, add11_2_p1, add11_3_p1, add11_4_g1);
  and and_8 (and_8_out, add11_2_p1, add11_3_p1, add11_4_p1, add11_4_c1[0]);
  and and_9 (and_9_out, add11_3_p1, add11_4_g1);
  and and_10 (and_10_out, add11_3_p1, add11_4_p1, add11_4_c1[0]);
  and and_11 (and_11_out, add11_4_p1, add11_4_c1[0]);
  and and_12 (p1, add11_1_p1, add11_2_p1, add11_3_p1, add11_4_p1);
  Button button_2 (.out(button_2_out));
  or or_1 (g1, add11_1_g1, and_2_out, and_3_out, and_4_out, and_5_out);
  or or_2 (or_4_out[3], add11_2_g1, and_6_out, and_7_out, and_8_out);
  or or_3 (or_4_out[2], add11_3_g1, and_9_out, and_10_out);
  or or_4 (or_4_out[1], add11_4_g1, and_11_out);
endmodule

module for4 (
  input  re,
  input  add1,
  output [3:0] cout
);

  wire or_1_out;

  Counter #(.max('hf), .width(4)) counter_1 (
    .load(re), .clk(or_1_out), .D(4'b0000), .Q(cout));  // open: clr, up, count, carry
  or or_1 (or_1_out, re, add1);
endmodule

module for441 (
  input  re,
  input  add1,
  output [3:0] f0,
  output [3:0] f4,
  output f8
);

  wire or_1_out;
  wire [3:0] undriven, undriven_2;
  wire [8:8] undriven_3;

  Counter #(.max('h1ff), .width(9)) counter_1 (
    .load(re), .clk(or_1_out), .D({undriven_3[8], undriven_2, undriven}), .Q({f8, f4, f0}));  // open: clr, up, count, carry
  or or_1 (or_1_out, re, add1);
endmodule
