// Logisim project 加法器.circ as structural Verilog
module add1bit (
  input  in_1,
  input  in_2,
  input  in_3,
  output out_4,
  output out_5
);

  wire and_1_out, and_2_out, xor_1_out;

  xor xor_1 (xor_1_out, in_1, in_2);
  and and_1 (and_1_out, xor_1_out, in_3);
  and and_2 (and_2_out, in_1, in_2);
  xor xor_2 (out_4, xor_1_out, in_3);
  or or_1 (out_5, and_1_out, and_2_out);
endmodule

module add4bit (
  input  [3:0] in_1,
  input  [3:0] in_2,
  output [3:0] out_3
);

  wire add1bit_1_out_5, add1bit_2_out_5, add1bit_3_out_5, add1bit_4_out_5;

  add1bit add1bit_1 (.in_1(in_1[0]), .in_2(in_2[0]), .in_3(1'b0), .out_4(out_3[0]), .out_5(add1bit_1_out_5));
  // Probe on out_3[0]
  add1bit add1bit_2 (.in_1(in_1[1]), .in_2(in_2[1]), .in_3(add1bit_1_out_5), .out_4(out_3[1]), .out_5(add1bit_2_out_5));
  // Probe on out_3[1]
  // Probe on out_3[2]
  add1bit add1bit_3 (.in_1(in_1[2]), .in_2(in_2[2]), .in_3(add1bit_2_out_5), .out_4(out_3[2]), .out_5(add1bit_3_out_5));
  // Probe on out_3[3]
  add1bit add1bit_4 (.in_1(in_1[3]), .in_2(in_2[3]), .in_3(add1bit_3_out_5), .out_4(out_3[3]), .out_5(add1bit_4_out_5));
endmodule
