// Logisim project work1.circ as structural Verilog
module reg99 (
  input  [4:0] choose0,
  input  [4:0] choose1,
  input  [4:0] choose2,
  input  cp,
  input  [31:0] c32,
  input  [31:0] i0,
  input  re,
  output [31:0] o0,
  output [31:0] o1,
  output [31:0] o2
);

  wire [31:0] register_1_q, register_2_q, register_3_q, register_4_q, register_5_q, register_6_q,
       register_7_q, register_8_q, register_9_q, register_10_q, register_11_q, register_12_q, register_13_q,
       register_14_q, register_15_q, register_16_q, register_17_q, register_18_q, register_19_q,
       register_20_q, register_21_q, register_22_q, register_23_q, register_24_q, register_25_q,
       register_26_q, register_27_q, register_28_q, register_29_q, register_30_q, register_31_q,
       register_32_q;

  Register #(.width(32)) register_1 (.D(i0), .en(c32[7]), .Q(register_1_q), .clk(cp), .clr(re));
  Register #(.width(32)) register_2 (.D(i0), .en(c32[15]), .Q(register_2_q), .clk(cp), .clr(re));
  Register #(.width(32)) register_3 (.D(i0), .en(c32[23]), .Q(register_3_q), .clk(cp), .clr(re));
  Register #(.width(32)) register_4 (.D(i0), .en(c32[31]), .Q(register_4_q), .clk(cp), .clr(re));
  Register #(.width(32)) register_5 (.D(i0), .en(c32[6]), .Q(register_5_q), .clk(cp), .clr(re));
  Register #(.width(32)) register_6 (.D(i0), .en(c32[14]), .Q(register_6_q), .clk(cp), .clr(re));
  Register #(.width(32)) register_7 (.D(i0), .en(c32[22]), .Q(register_7_q), .clk(cp), .clr(re));
  Register #(.width(32)) register_8 (.D(i0), .en(c32[30]), .Q(register_8_q), .clk(cp), .clr(re));
  Register #(.width(32)) register_9 (.D(i0), .en(c32[5]), .Q(register_9_q), .clk(cp), .clr(re));
  Register #(.width(32)) register_10 (.D(i0), .en(c32[13]), .Q(register_10_q), .clk(cp), .clr(re));
  Register #(.width(32)) register_11 (.D(i0), .en(c32[21]), .Q(register_11_q), .clk(cp), .clr(re));
  Register #(.width(32)) register_12 (.D(i0), .en(c32[29]), .Q(register_12_q), .clk(cp), .clr(re));
  Register #(.width(32)) register_13 (.D(i0), .en(c32[4]), .Q(register_13_q), .clk(cp), .clr(re));
  Register #(.width(32)) register_14 (.D(i0), .en(c32[12]), .Q(register_14_q), .clk(cp), .clr(re));
  Register #(.width(32)) register_15 (.D(i0), .en(c32[20]), .Q(register_15_q), .clk(cp), .clr(re));
  Register #(.width(32)) register_16 (.D(i0), .en(c32[28]), .Q(register_16_q), .clk(cp), .clr(re));
  Register #(.width(32)) register_17 (.D(i0), .en(c32[3]), .Q(register_17_q), .clk(cp), .clr(re));
  Register #(.width(32)) register_18 (.D(i0), .en(c32[2]), .Q(register_18_q), .clk(cp), .clr(re));
  Register #(.width(32)) register_19 (.D(i0), .en(c32[11]), .Q(register_19_q), .clk(cp), .clr(re));
  Register #(.width(32)) register_20 (.D(i0), .en(c32[10]), .Q(register_20_q), .clk(cp), .clr(re));
  Register #(.width(32)) register_21 (.D(i0), .en(c32[19]), .Q(register_21_q), .clk(cp), .clr(re));
  Register #(.width(32)) register_22 (.D(i0), .en(c32[18]), .Q(register_22_q), .clk(cp), .clr(re));
  Register #(.width(32)) register_23 (.D(i0), .en(c32[27]), .Q(register_23_q), .clk(cp), .clr(re));
  Register #(.width(32)) register_24 (.D(i0), .en(c32[26]), .Q(register_24_q), .clk(cp), .clr(re));
  Register #(.width(32)) register_25 (.D(i0), .en(c32[1]), .Q(register_25_q), .clk(cp), .clr(re));
  Register #(.width(32)) register_26 (.D(i0), .en(c32[9]), .Q(register_26_q), .clk(cp), .clr(re));
  Register #(.width(32)) register_27 (.D(i0), .en(c32[17]), .Q(register_27_q), .clk(cp), .clr(re));
  Register #(.width(32)) register_28 (.D(i0), .en(c32[25]), .Q(register_28_q), .clk(cp), .clr(re));
  Register #(.width(32)) register_29 (.D(i0), .en(c32[0]), .Q(register_29_q), .clk(cp), .clr(re));
  Register #(.width(32)) register_30 (.D(i0), .en(c32[8]), .Q(register_30_q), .clk(cp), .clr(re));
  Register #(.width(32)) register_31 (.D(i0), .en(c32[16]), .Q(register_31_q), .clk(cp), .clr(re));
  Register #(.width(32)) register_32 (.D(i0), .en(c32[24]), .Q(register_32_q), .clk(cp), .clr(re));
  Multiplexer #(.enable("false"), .select(5), .width(32)) multiplexer_1 (
    .in0(register_29_q), .in1(register_25_q), .in2(register_18_q), .in3(register_17_q), .in4(register_13_q),
    .in5(register_9_q), .in6(register_5_q), .in7(register_1_q), .in8(register_30_q), .in9(register_26_q),
    .in10(register_20_q), .in11(register_19_q), .in12(register_14_q), .in13(register_10_q),
    .in14(register_6_q), .in15(register_2_q), .in16(register_31_q), .in17(register_27_q),
    .in18(register_22_q), .in19(register_21_q), .in20(register_15_q), .in21(register_11_q),
    .in22(register_7_q), .in23(register_3_q), .in24(register_32_q), .in25(register_28_q),
    .in26(register_24_q), .in27(register_23_q), .in28(register_16_q), .in29(register_12_q),
    .in30(register_8_q), .in31(register_4_q), .out(o0), .sel(choose0));
  Multiplexer #(.enable("false"), .select(5), .width(32)) multiplexer_2 (
    .in0(register_29_q), .in1(register_25_q), .in2(register_18_q), .in3(register_17_q), .in4(register_13_q),
    .in5(register_9_q), .in6(register_5_q), .in7(register_1_q), .in8(register_30_q), .in9(register_26_q),
    .in10(register_20_q), .in11(register_19_q), .in12(register_14_q), .in13(register_10_q),
    .in14(register_6_q), .in15(register_2_q), .in16(register_31_q), .in17(register_27_q),
    .in18(register_22_q), .in19(register_21_q), .in20(register_15_q), .in21(register_11_q),
    .in22(register_7_q), .in23(register_3_q), .in24(register_32_q), .in25(register_28_q),
    .in26(register_24_q), .in27(register_23_q), .in28(register_16_q), .in29(register_12_q),
    .in30(register_8_q), .in31(register_4_q), .out(o1), .sel(choose1));
  Multiplexer #(.enable("false"), .select(5), .width(32)) multiplexer_3 (
    .in0(register_29_q), .in1(register_25_q), .in2(register_18_q), .in3(register_17_q), .in4(register_13_q),
    .in5(register_9_q), .in6(register_5_q), .in7(register_1_q), .in8(register_30_q), .in9(register_26_q),
    .in10(register_20_q), .in11(register_19_q), .in12(register_14_q), .in13(register_10_q),
    .in14(register_6_q), .in15(register_2_q), .in16(register_31_q), .in17(register_27_q),
    .in18(register_22_q), .in19(register_21_q), .in20(register_15_q), .in21(register_11_q),
    .in22(register_7_q), .in23(register_3_q), .in24(register_32_q), .in25(register_28_q),
    .in26(register_24_q), .in27(register_23_q), .in28(register_16_q), .in29(register_12_q),
    .in30(register_8_q), .in31(register_4_q), .out(o2), .sel(choose2));
endmodule

module mux121 (
  input  a,
  input  b,
  input  s,
  output c
);

  wire and_1_out, and_2_out, not_1_out;

  not not_1 (not_1_out, s);
  and and_1 (and_1_out, not_1_out, a);
  and and_2 (and_2_out, b, s);
  or or_1 (c, and_1_out, and_2_out);
  // Probe on c
endmodule

module muxx1632 (
  input  [31:0] a0,
  input  [31:0] in_2,
  input  [31:0] in_3,
  input  [31:0] in_4,
  input  [31:0] a4,
  input  [31:0] in_6,
  input  [31:0] in_7,
  input  [31:0] in_8,
  input  [31:0] a8,
  input  [31:0] in_10,
  input  [31:0] in_11,
  input  [31:0] in_12,
  input  [31:0] a12,
  input  [31:0] in_14,
  input  [31:0] in_15,
  input  [31:0] a15,
  input  [31:0] x,
  input  [3:0] choose,
  input  re0,
  output [31:0] b0,
  output [31:0] out_21,
  output [31:0] out_22,
  output [31:0] out_23,
  output [31:0] b4,
  output [31:0] out_25,
  output [31:0] out_26,
  output [31:0] out_27,
  output [31:0] b8,
  output [31:0] out_29,
  output [31:0] out_30,
  output [31:0] out_31,
  output [31:0] b12,
  output [31:0] out_33,
  output [31:0] out_34,
  output [31:0] b15
);

  wire [15:0] demultiplexer_1_out0, or_1_out;
  wire [31:0] and_1_out;
  wire [31:31] not_1_out;

  Demultiplexer #(.enable("false"), .select(4)) demultiplexer_1 (
    .out0(demultiplexer_1_out0[0]), .out1(demultiplexer_1_out0[1]), .out2(demultiplexer_1_out0[2]),
    .out3(demultiplexer_1_out0[3]), .out4(demultiplexer_1_out0[4]), .out5(demultiplexer_1_out0[5]),
    .out6(demultiplexer_1_out0[6]), .out7(demultiplexer_1_out0[7]), .out8(demultiplexer_1_out0[8]),
    .out9(demultiplexer_1_out0[9]), .out10(demultiplexer_1_out0[10]), .out11(demultiplexer_1_out0[11]),
    .out12(demultiplexer_1_out0[12]), .out13(demultiplexer_1_out0[13]), .out14(demultiplexer_1_out0[14]),
    .out15(demultiplexer_1_out0[15]), .in(1'b1), .sel(choose));
  assign or_1_out = demultiplexer_1_out0 | {16{re0}};  // OR_Gate or_1, 16 bits wide
  not not_1 (not_1_out[31], re0);
  assign and_1_out = x & {32{not_1_out[31]}};  // AND_Gate and_1, 32 bits wide
  // Probe on and_1_out
  Multiplexer #(.enable("false"), .width(32)) multiplexer_1 (.in0(a0), .in1(and_1_out), .out(b0), .sel(or_1_out[0]));
  Multiplexer #(.enable("false"), .width(32)) multiplexer_2 (
    .in0(in_2), .in1(and_1_out), .out(out_21), .sel(or_1_out[1]));
  Multiplexer #(.enable("false"), .width(32)) multiplexer_3 (
    .in0(in_3), .in1(and_1_out), .out(out_22), .sel(or_1_out[2]));
  Multiplexer #(.enable("false"), .width(32)) multiplexer_4 (
    .in0(in_4), .in1(and_1_out), .out(out_23), .sel(or_1_out[3]));
  Multiplexer #(.enable("false"), .width(32)) multiplexer_5 (.in0(a4), .in1(and_1_out), .out(b4), .sel(or_1_out[4]));
  Multiplexer #(.enable("false"), .width(32)) multiplexer_6 (
    .in0(in_6), .in1(and_1_out), .out(out_25), .sel(or_1_out[5]));
  Multiplexer #(.enable("false"), .width(32)) multiplexer_7 (
    .in0(in_7), .in1(and_1_out), .out(out_26), .sel(or_1_out[6]));
  Multiplexer #(.enable("false"), .width(32)) multiplexer_8 (
    .in0(in_8), .in1(and_1_out), .out(out_27), .sel(or_1_out[7]));
  Multiplexer #(.enable("false"), .width(32)) multiplexer_9 (.in0(a8), .in1(and_1_out), .out(b8), .sel(or_1_out[8]));
  Multiplexer #(.enable("false"), .width(32)) multiplexer_10 (
    .in0(in_10), .in1(and_1_out), .out(out_29), .sel(or_1_out[9]));
  Multiplexer #(.enable("false"), .width(32)) multiplexer_11 (
    .in0(in_11), .in1(and_1_out), .out(out_30), .sel(or_1_out[10]));
  Multiplexer #(.enable("false"), .width(32)) multiplexer_12 (
    .in0(in_12), .in1(and_1_out), .out(out_31), .sel(or_1_out[11]));
  Multiplexer #(.enable("false"), .width(32)) multiplexer_13 (
    .in0(a12), .in1(and_1_out), .out(b12), .sel(or_1_out[12]));
  Multiplexer #(.enable("false"), .width(32)) multiplexer_14 (
    .in0(in_14), .in1(and_1_out), .out(out_33), .sel(or_1_out[13]));
  Multiplexer #(.enable("false"), .width(32)) multiplexer_15 (
    .in0(in_15), .in1(and_1_out), .out(out_34), .sel(or_1_out[14]));
  Multiplexer #(.enable("false"), .width(32)) multiplexer_16 (
    .in0(a15), .in1(and_1_out), .out(b15), .sel(or_1_out[15]));
endmodule

module gpr16 (
  input  [31:0] Wd,
  input  Regwrite,
  input  Clk,
  input  Reset,
  input  [3:0] A1,
  input  [3:0] A2,
  input  [3:0] A3,
  output [31:0] Rd1,
  output [31:0] Rd2
);

  wire shift_register_1_p1, shift_register_1_p2, shift_register_1_p4;
  wire [31:0] muxx1632_1_b12, muxx1632_1_b15, muxx1632_1_out_33, muxx1632_1_out_34, shift_register_1_p7,
       shift_register_1_p8, shift_register_1_p9, shift_register_1_p10, shift_register_1_p11,
       shift_register_1_p12, shift_register_1_p13, shift_register_1_p14, shift_register_1_p15,
       shift_register_1_p16, shift_register_1_p17, shift_register_1_p18, shift_register_1_p19,
       shift_register_1_p20, shift_register_1_p21, shift_register_1_p22, shift_register_1_p23,
       shift_register_1_p24, shift_register_1_p25, shift_register_1_p26, shift_register_1_p27,
       shift_register_1_p28, shift_register_1_p29, shift_register_1_p30, undriven, undriven_2, undriven_3,
       undriven_4;

  // Shift_Register #(.length(16), .width(32)) shift_register_1: pin names not known; wires that end beside it: shift_register_1_p1, shift_register_1_p2, Regwrite, shift_register_1_p4, Clk, shift_register_1_p1, shift_register_1_p7, shift_register_1_p8, shift_register_1_p9, shift_register_1_p10, shift_register_1_p11, shift_register_1_p12, shift_register_1_p13, shift_register_1_p14, shift_register_1_p15, shift_register_1_p16, shift_register_1_p17, shift_register_1_p18, shift_register_1_p19, shift_register_1_p20, shift_register_1_p21, shift_register_1_p22, shift_register_1_p23, shift_register_1_p24, shift_register_1_p25, shift_register_1_p26, shift_register_1_p27, shift_register_1_p28, shift_register_1_p29, shift_register_1_p30
  muxx1632 muxx1632_1 (
    .a0(shift_register_1_p19), .in_2(shift_register_1_p20), .in_3(shift_register_1_p21),
    .in_4(shift_register_1_p22), .a4(shift_register_1_p23), .in_6(shift_register_1_p24),
    .in_7(shift_register_1_p25), .in_8(shift_register_1_p26), .a8(shift_register_1_p27),
    .in_10(shift_register_1_p28), .in_11(shift_register_1_p29), .in_12(shift_register_1_p30), .a12(undriven),
    .in_14(undriven_2), .in_15(undriven_3), .a15(undriven_4), .x(Wd), .choose(A3), .re0(Reset),
    .b0(shift_register_1_p7), .out_21(shift_register_1_p8), .out_22(shift_register_1_p9),
    .out_23(shift_register_1_p10), .b4(shift_register_1_p11), .out_25(shift_register_1_p12),
    .out_26(shift_register_1_p13), .out_27(shift_register_1_p14), .b8(shift_register_1_p15),
    .out_29(shift_register_1_p16), .out_30(shift_register_1_p17), .out_31(shift_register_1_p18),
    .b12(muxx1632_1_b12), .out_33(muxx1632_1_out_33), .out_34(muxx1632_1_out_34), .b15(muxx1632_1_b15));
  Multiplexer #(.enable("false"), .select(4), .width(32)) multiplexer_1 (
    .in0(shift_register_1_p19), .in1(shift_register_1_p20), .in2(shift_register_1_p21),
    .in3(shift_register_1_p22), .in4(shift_register_1_p23), .in5(shift_register_1_p24),
    .in6(shift_register_1_p25), .in7(shift_register_1_p26), .in8(shift_register_1_p27),
    .in9(shift_register_1_p28), .in10(shift_register_1_p29), .in11(shift_register_1_p30), .in12(undriven),
    .in13(undriven_2), .in14(undriven_3), .in15(undriven_4), .out(Rd1), .sel(A1));
  Multiplexer #(.enable("false"), .select(4), .width(32)) multiplexer_2 (
    .in0(shift_register_1_p19), .in1(shift_register_1_p20), .in2(shift_register_1_p21),
    .in3(shift_register_1_p22), .in4(shift_register_1_p23), .in5(shift_register_1_p24),
    .in6(shift_register_1_p25), .in7(shift_register_1_p26), .in8(shift_register_1_p27),
    .in9(shift_register_1_p28), .in10(shift_register_1_p29), .in11(shift_register_1_p30), .in12(undriven),
    .in13(undriven_2), .in14(undriven_3), .in15(undriven_4), .out(Rd2), .sel(A2));
endmodule

module add2 (
  input  in_1,
  input  in_2,
  input  in_3,
  input  in_4,
  input  in_5
);

  wire add1_1_c1, add1_1_g1, add1_1_p1, add1_1_sigma, add1_2_g1, add1_2_p1, add1_2_sigma, and_1_out,
       and_2_out, and_3_out, or_1_out, or_2_out;

  add1 add1_1 (.a(in_1), .b(in_2), .c0(or_2_out), .p1(add1_1_p1), .sigma(add1_1_sigma), .c1(add1_1_c1), .g1(add1_1_g1));
  add1 add1_2 (.a(in_3), .b(in_4), .c0(in_5), .p1(add1_2_p1), .sigma(add1_2_sigma), .g1(add1_2_g1));  // open: c1
  and and_1 (and_1_out, add1_1_p1, add1_1_c1);
  and and_2 (and_2_out, add1_1_p1, add1_2_p1, in_5);
  and and_3 (and_3_out, add1_2_p1, in_5);
  or or_1 (or_1_out, add1_1_g1, and_1_out, and_2_out);
  or or_2 (or_2_out, and_3_out, add1_2_g1);
endmodule

module add64 (
  input  [63:0] in_1,
  input  [63:0] in_2,
  input  in_3,
  output gg16,
  output [63:0] sigma,
  output c64,
  output pp16
);

  wire add16_1_gg4, add16_1_pp4, add16_2_gg4, add16_2_pp4, add16_3_gg4, add16_3_pp4, add16_4_gg4,
       add16_4_pp4, adder_1_cout, and_1_out, and_2_out, and_3_out, and_4_out, and_5_out, and_6_out,
       and_7_out, and_8_out, and_9_out, and_10_out, and_11_out, comparator_1_eq, comparator_2_eq, not_1_out,
       undriven_3;
  wire [3:0] add16_4_c16;
  wire [3:1] or_4_out;
  wire [15:0] multiplexer_1_out, multiplexer_1_out_2, multiplexer_1_out_3, multiplexer_1_out_4,
       multiplexer_2_out, multiplexer_2_out_2, multiplexer_2_out_3;
  wire [63:0] adder_1_out, undriven, undriven_2;
  wire [63:48] multiplexer_2_out_4;

  Multiplexer #(.enable("false"), .width(64)) multiplexer_1 (
    .in0(in_1), .in1(undriven_2),
    .out({multiplexer_1_out_4, multiplexer_1_out_3, multiplexer_1_out_2, multiplexer_1_out}), .sel(1'b0));
  Multiplexer #(.enable("false"), .width(64)) multiplexer_2 (
    .in0(in_2), .in1(undriven),
    .out({multiplexer_2_out_4, multiplexer_2_out_3, multiplexer_2_out_2, multiplexer_2_out}), .sel(1'b0));
  // Probe on {multiplexer_1_out_4, multiplexer_1_out_3, multiplexer_1_out_2, multiplexer_1_out}
  Adder #(.width(64)) adder_1 (
    .a({multiplexer_1_out_4, multiplexer_1_out_3, multiplexer_1_out_2, multiplexer_1_out}),
    .b({multiplexer_2_out_4, multiplexer_2_out_3, multiplexer_2_out_2, multiplexer_2_out}),
    .out(adder_1_out), .cin(add16_4_c16[0]), .cout(adder_1_cout));
  // Probe on {multiplexer_2_out_4, multiplexer_2_out_3, multiplexer_2_out_2, multiplexer_2_out}
  // Probe on {c64, add16_4_c16}
  // Probe on {gg16, or_4_out, add16_4_c16[0]}
  // Probe on adder_1_out
  // Probe on sigma
  // Probe on adder_1_cout
  // Probe on c64
  Comparator #(.width(64)) comparator_1 (.a(sigma), .b(adder_1_out), .eq(comparator_1_eq));  // open: gt, lt
  add16 add16_1 (
    .a(multiplexer_2_out_4), .b(multiplexer_1_out_4), .c0(or_4_out[3]), .pp4(add16_1_pp4),
    .sigma(sigma[63:48]), .c16(c64), .gg4(add16_1_gg4));
  add16 add16_2 (
    .a(multiplexer_2_out_3), .b(multiplexer_1_out_3), .c0(or_4_out[2]), .pp4(add16_2_pp4),
    .sigma(sigma[47:32]), .c16(add16_4_c16[3]), .gg4(add16_2_gg4));
  add16 add16_3 (
    .a(multiplexer_2_out_2), .b(multiplexer_1_out_2), .c0(or_4_out[1]), .pp4(add16_3_pp4),
    .sigma(sigma[31:16]), .c16(add16_4_c16[2]), .gg4(add16_3_gg4));
  add16 add16_4 (
    .a(multiplexer_2_out), .b(multiplexer_1_out), .c0(add16_4_c16[0]), .pp4(add16_4_pp4),
    .sigma(sigma[15:0]), .c16(add16_4_c16[1]), .gg4(add16_4_gg4));
  Comparator #(.width(5)) comparator_2 (
    .a({c64, add16_4_c16}), .b({gg16, or_4_out, add16_4_c16[0]}), .eq(comparator_2_eq));  // open: gt, lt
  Multiplexer #(.enable("false")) multiplexer_3 (.in0(in_3), .in1(undriven_3), .out(add16_4_c16[0]), .sel(1'b0));
  and and_1 (and_1_out, comparator_2_eq, comparator_1_eq);
  LED led_1 (.in(and_1_out));
  not not_1 (not_1_out, and_1_out);
  LED led_2 (.in(not_1_out));
  and and_2 (and_2_out, add16_1_pp4, add16_2_gg4);
  and and_3 (and_3_out, add16_1_pp4, add16_2_pp4, add16_3_gg4);
  and and_4 (and_4_out, add16_1_pp4, add16_2_pp4, add16_3_pp4, add16_4_gg4);
  and and_5 (and_5_out, add16_1_pp4, add16_2_pp4, add16_3_pp4, add16_4_pp4, add16_4_c16[0]);
  and and_6 (and_6_out, add16_2_pp4, add16_3_gg4);
  and and_7 (and_7_out, add16_2_pp4, add16_3_pp4, add16_4_gg4);
  and and_8 (and_8_out, add16_2_pp4, add16_3_pp4, add16_4_pp4, add16_4_c16[0]);
  and and_9 (and_9_out, add16_3_pp4, add16_4_gg4);
  and and_10 (and_10_out, add16_3_pp4, add16_4_pp4, add16_4_c16[0]);
  and and_11 (and_11_out, add16_4_pp4, add16_4_c16[0]);
  and and_12 (pp16, add16_1_pp4, add16_2_pp4, add16_3_pp4, add16_4_pp4);
  or or_1 (gg16, add16_1_gg4, and_2_out, and_3_out, and_4_out, and_5_out);
  or or_2 (or_4_out[3], add16_2_gg4, and_6_out, and_7_out, and_8_out);
  or or_3 (or_4_out[2], add16_3_gg4, and_9_out, and_10_out);
  or or_4 (or_4_out[1], add16_4_gg4, and_11_out);
endmodule

module for4 (
  input  re,
  input  add1,
  output [3:0] cout
);

  wire or_1_out;

  Counter #(.max('hf), .width(4)) counter_1 (
    .load(re), .clk(or_1_out), .D(4'b0000), .Q(cout));  // open: clr, up, count, carry
  or or_1 (or_1_out, re, add1);
endmodule

module for9 (
  input  re,
  input  add1,
  output [3:0] f0,
  output [3:0] f4,
  output f8
);

  wire or_1_out;
  wire [3:0] undriven, undriven_2;
  wire [8:8] undriven_3;

  Counter #(.max('h1ff), .width(9)) counter_1 (
    .load(re), .clk(or_1_out), .D({undriven_3[8], undriven_2, undriven}), .Q({f8, f4, f0}));  // open: clr, up, count, carry
  or or_1 (or_1_out, re, add1);
endmodule

module add1 (
  input  a,
  input  b,
  input  c0,
  output p1,
  output sigma,
  output c1,
  output g1
);

  wire and_2_out;

  xor xor_1 (p1, a, b);
  and and_1 (g1, a, b);
  and and_2 (and_2_out, p1, c0);
  xor xor_2 (sigma, p1, c0);
  or or_1 (c1, and_2_out, g1);
endmodule

module add4 (
  input  [3:0] a,
  input  [3:0] b,
  input  c0,
  output pp1,
  output [3:0] sigma,
  output c4,
  output gg1
);

  wire add1_1_g1, add1_1_p1, add1_2_g1, add1_2_p1, add1_3_g1, add1_3_p1, add1_4_g1, add1_4_p1, adder_1_cout,
       and_1_out, and_2_out, and_3_out, and_4_out, and_5_out, and_6_out, and_7_out, and_8_out, and_9_out,
       and_10_out, and_11_out, button_1_out, button_2_out, comparator_1_eq, comparator_2_eq, for9_1_f8,
       not_1_out;
  wire [3:0] add1_4_c1, adder_1_out, for9_1_f0, for9_1_f4, multiplexer_1_out, multiplexer_2_out;
  wire [3:1] or_4_out;

  Multiplexer #(.enable("false"), .width(4)) multiplexer_1 (
    .in0(a), .in1(for9_1_f4), .out(multiplexer_1_out), .sel(1'b0));
  Multiplexer #(.enable("false"), .width(4)) multiplexer_2 (
    .in0(b), .in1(for9_1_f0), .out(multiplexer_2_out), .sel(1'b0));
  // Probe on multiplexer_1_out
  Adder #(.width(4)) adder_1 (
    .a(multiplexer_1_out), .b(multiplexer_2_out), .out(adder_1_out), .cin(add1_4_c1[0]), .cout(adder_1_cout));
  // Probe on multiplexer_2_out
  // Probe on {c4, add1_4_c1}
  // Probe on {gg1, or_4_out, add1_4_c1[0]}
  // Probe on adder_1_out
  // Probe on sigma
  // Probe on adder_1_cout
  // Probe on c4
  Comparator #(.width(4)) comparator_1 (.a(sigma), .b(adder_1_out), .eq(comparator_1_eq));  // open: gt, lt
  add1 add1_1 (
    .a(multiplexer_2_out[3]), .b(multiplexer_1_out[3]), .c0(or_4_out[3]), .p1(add1_1_p1), .sigma(sigma[3]),
    .c1(c4), .g1(add1_1_g1));
  add1 add1_2 (
    .a(multiplexer_2_out[2]), .b(multiplexer_1_out[2]), .c0(or_4_out[2]), .p1(add1_2_p1), .sigma(sigma[2]),
    .c1(add1_4_c1[3]), .g1(add1_2_g1));
  add1 add1_3 (
    .a(multiplexer_2_out[1]), .b(multiplexer_1_out[1]), .c0(or_4_out[1]), .p1(add1_3_p1), .sigma(sigma[1]),
    .c1(add1_4_c1[2]), .g1(add1_3_g1));
  add1 add1_4 (
    .a(multiplexer_2_out[0]), .b(multiplexer_1_out[0]), .c0(add1_4_c1[0]), .p1(add1_4_p1), .sigma(sigma[0]),
    .c1(add1_4_c1[1]), .g1(add1_4_g1));
  Comparator #(.width(5)) comparator_2 (
    .a({c4, add1_4_c1}), .b({gg1, or_4_out, add1_4_c1[0]}), .eq(comparator_2_eq));  // open: gt, lt
  Multiplexer #(.enable("false")) multiplexer_3 (.in0(c0), .in1(for9_1_f8), .out(add1_4_c1[0]), .sel(1'b0));
  for9 for9_1 (.re(button_1_out), .add1(button_2_out), .f0(for9_1_f0), .f4(for9_1_f4), .f8(for9_1_f8));
  and and_1 (and_1_out, comparator_2_eq, comparator_1_eq);
  LED led_1 (.in(and_1_out));
  not not_1 (not_1_out, and_1_out);
  LED led_2 (.in(not_1_out));
  Button button_1 (.out(button_1_out));
  and and_2 (and_2_out, add1_1_p1, add1_2_g1);
  and and_3 (and_3_out, add1_1_p1, add1_2_p1, add1_3_g1);
  and and_4 (and_4_out, add1_1_p1, add1_2_p1, add1_3_p1, add1_4_g1);
  and and_5 (and_5_out, add1_1_p1, add1_2_p1, add1_3_p1, add1_4_p1, add1_4_c1[0]);
  and and_6 (and_6_out, add1_2_p1, add1_3_g1);
  and and_7 (and_7_out, add1_2_p1, add1_3_p1, add1_4_g1);
  and and_8 (and_8_out, add1_2_p1, add1_3_p1, add1_4_p1, add1_4_c1[0]);
  and and_9 (and_9_out, add1_3_p1, add1_4_g1);
  and and_10 (and_10_out, add1_3_p1, add1_4_p1, add1_4_c1[0]);
  and and_11 (and_11_out, add1_4_p1, add1_4_c1[0]);
  and and_12 (pp1, add1_1_p1, add1_2_p1, add1_3_p1, add1_4_p1);
  Button button_2 (.out(button_2_out));
  or or_1 (gg1, add1_1_g1, and_2_out, and_3_out, and_4_out, and_5_out);
  or or_2 (or_4_out[3], add1_2_g1, and_6_out, and_7_out, and_8_out);
  or or_3 (or_4_out[2], add1_3_g1, and_9_out, and_10_out);
  or or_4 (or_4_out[1], add1_4_g1, and_11_out);
endmodule

module add16 (
  input  [15:0] a,
  input  [15:0] b,
  input  c0,
  output pp4,
  output [15:0] sigma,
  output c16,
  output gg4
);

  wire add4_1_gg1, add4_1_pp1, add4_2_gg1, add4_2_pp1, add4_3_gg1, add4_3_pp1, add4_4_gg1, add4_4_pp1,
       adder_1_cout, and_1_out, and_2_out, and_3_out, and_4_out, and_5_out, and_6_out, and_7_out, and_8_out,
       and_9_out, and_10_out, and_11_out, comparator_1_eq, comparator_2_eq, not_1_out;
  wire [3:1] add4_4_c4, or_4_out;
  wire [15:0] adder_1_out;

  // Probe on a
  Adder #(.width(16)) adder_1 (.a(a), .b(b), .out(adder_1_out), .cin(c0), .cout(adder_1_cout));
  // Probe on b
  // Probe on {c16, add4_4_c4, c0}
  // Probe on {gg4, or_4_out, c0}
  // Probe on adder_1_out
  // Probe on sigma
  // Probe on adder_1_cout
  // Probe on c16
  Comparator #(.width(16)) comparator_1 (.a(sigma), .b(adder_1_out), .eq(comparator_1_eq));  // open: gt, lt
  add4 add4_1 (
    .a(b[15:12]), .b(a[15:12]), .c0(or_4_out[3]), .pp1(add4_1_pp1), .sigma(sigma[15:12]), .c4(c16),
    .gg1(add4_1_gg1));
  add4 add4_2 (
    .a(b[11:8]), .b(a[11:8]), .c0(or_4_out[2]), .pp1(add4_2_pp1), .sigma(sigma[11:8]), .c4(add4_4_c4[3]),
    .gg1(add4_2_gg1));
  add4 add4_3 (
    .a(b[7:4]), .b(a[7:4]), .c0(or_4_out[1]), .pp1(add4_3_pp1), .sigma(sigma[7:4]), .c4(add4_4_c4[2]),
    .gg1(add4_3_gg1));
  add4 add4_4 (
    .a(b[3:0]), .b(a[3:0]), .c0(c0), .pp1(add4_4_pp1), .sigma(sigma[3:0]), .c4(add4_4_c4[1]), .gg1(add4_4_gg1));
  Comparator #(.width(5)) comparator_2 (
    .a({c16, add4_4_c4, c0}), .b({gg4, or_4_out, c0}), .eq(comparator_2_eq));  // open: gt, lt
  and and_1 (and_1_out, comparator_2_eq, comparator_1_eq);
  LED led_1 (.in(and_1_out));
  not not_1 (not_1_out, and_1_out);
  LED led_2 (.in(not_1_out));
  and and_2 (and_2_out, add4_1_pp1, add4_2_gg1);
  and and_3 (and_3_out, add4_1_pp1, add4_2_pp1, add4_3_gg1);
  and and_4 (and_4_out, add4_1_pp1, add4_2_pp1, add4_3_pp1, add4_4_gg1);
  and and_5 (and_5_out, add4_1_pp1, add4_2_pp1, add4_3_pp1, add4_4_pp1, c0);
  and and_6 (and_6_out, add4_2_pp1, add4_3_gg1);
  and and_7 (and_7_out, add4_2_pp1, add4_3_pp1, add4_4_gg1);
  and and_8 (and_8_out, add4_2_pp1, add4_3_pp1, add4_4_pp1, c0);
  and and_9 (and_9_out, add4_3_pp1, add4_4_gg1);
  and and_10 (and_10_out, add4_3_pp1, add4_4_pp1, c0);
  and and_11 (and_11_out, add4_4_pp1, c0);
  and and_12 (pp4, add4_1_pp1, add4_2_pp1, add4_3_pp1, add4_4_pp1);
  or or_1 (gg4, add4_1_gg1, and_2_out, and_3_out, and_4_out, and_5_out);
  or or_2 (or_4_out[3], add4_2_gg1, and_6_out, and_7_out, and_8_out);
  or or_3 (or_4_out[2], add4_3_gg1, and_9_out, and_10_out);
  or or_4 (or_4_out[1], add4_4_gg1, and_11_out);
endmodule

module add32 (
  input  c0,
  input  [31:0] a,
  input  [31:0] b,
  output c32,
  output [31:0] sigma
);

  wire add16_1_gg4, add16_1_pp4, add16_2_gg4, add16_2_pp4, and_1_out, and_2_out, and_3_out, or_2_out;

  add16 add16_1 (
    .a(a[31:16]), .b(b[31:16]), .c0(or_2_out), .pp4(add16_1_pp4), .sigma(sigma[31:16]), .gg4(add16_1_gg4));  // open: c16
  add16 add16_2 (
    .a(a[15:0]), .b(b[15:0]), .c0(c0), .pp4(add16_2_pp4), .sigma(sigma[15:0]), .gg4(add16_2_gg4));  // open: c16
  and and_1 (and_1_out, add16_1_pp4, add16_2_gg4);
  and and_2 (and_2_out, add16_1_pp4, add16_2_pp4, c0);
  and and_3 (and_3_out, add16_2_pp4, c0);
  or or_1 (c32, add16_1_gg4, and_1_out, and_2_out);
  or or_2 (or_2_out, and_3_out, add16_2_gg4);
endmodule

module reg32 (
  input  [4:0] choose0,
  input  [4:0] choose1,
  input  cp,
  input  [31:0] i0,
  input  re,
  input  [31:0] c32,
  output [31:0] o0,
  output [31:0] o1
);

  wire [31:0] register_1_q, register_2_q, register_3_q, register_4_q, register_5_q, register_6_q,
       register_7_q, register_8_q, register_9_q, register_10_q, register_11_q, register_12_q, register_13_q,
       register_14_q, register_15_q, register_16_q, register_17_q, register_18_q, register_19_q,
       register_20_q, register_21_q, register_22_q, register_23_q, register_24_q, register_25_q,
       register_26_q, register_27_q, register_28_q, register_29_q, register_30_q, register_31_q,
       register_32_q;

  Register #(.width(32)) register_1 (.D(i0), .en(c32[7]), .Q(register_1_q), .clk(cp), .clr(re));
  Register #(.width(32)) register_2 (.D(i0), .en(c32[15]), .Q(register_2_q), .clk(cp), .clr(re));
  Register #(.width(32)) register_3 (.D(i0), .en(c32[23]), .Q(register_3_q), .clk(cp), .clr(re));
  Register #(.width(32)) register_4 (.D(i0), .en(c32[31]), .Q(register_4_q), .clk(cp), .clr(re));
  Register #(.width(32)) register_5 (.D(i0), .en(c32[6]), .Q(register_5_q), .clk(cp), .clr(re));
  Register #(.width(32)) register_6 (.D(i0), .en(c32[14]), .Q(register_6_q), .clk(cp), .clr(re));
  Register #(.width(32)) register_7 (.D(i0), .en(c32[22]), .Q(register_7_q), .clk(cp), .clr(re));
  Register #(.width(32)) register_8 (.D(i0), .en(c32[30]), .Q(register_8_q), .clk(cp), .clr(re));
  Register #(.width(32)) register_9 (.D(i0), .en(c32[5]), .Q(register_9_q), .clk(cp), .clr(re));
  Register #(.width(32)) register_10 (.D(i0), .en(c32[13]), .Q(register_10_q), .clk(cp), .clr(re));
  Register #(.width(32)) register_11 (.D(i0), .en(c32[21]), .Q(register_11_q), .clk(cp), .clr(re));
  Register #(.width(32)) register_12 (.D(i0), .en(c32[29]), .Q(register_12_q), .clk(cp), .clr(re));
  Register #(.width(32)) register_13 (.D(i0), .en(c32[4]), .Q(register_13_q), .clk(cp), .clr(re));
  Register #(.width(32)) register_14 (.D(i0), .en(c32[12]), .Q(register_14_q), .clk(cp), .clr(re));
  Register #(.width(32)) register_15 (.D(i0), .en(c32[20]), .Q(register_15_q), .clk(cp), .clr(re));
  Register #(.width(32)) register_16 (.D(i0), .en(c32[28]), .Q(register_16_q), .clk(cp), .clr(re));
  Register #(.width(32)) register_17 (.D(i0), .en(c32[3]), .Q(register_17_q), .clk(cp), .clr(re));
  Register #(.width(32)) register_18 (.D(i0), .en(c32[2]), .Q(register_18_q), .clk(cp), .clr(re));
  Register #(.width(32)) register_19 (.D(i0), .en(c32[11]), .Q(register_19_q), .clk(cp), .clr(re));
  Register #(.width(32)) register_20 (.D(i0), .en(c32[10]), .Q(register_20_q), .clk(cp), .clr(re));
  Register #(.width(32)) register_21 (.D(i0), .en(c32[19]), .Q(register_21_q), .clk(cp), .clr(re));
  Register #(.width(32)) register_22 (.D(i0), .en(c32[18]), .Q(register_22_q), .clk(cp), .clr(re));
  Register #(.width(32)) register_23 (.D(i0), .en(c32[27]), .Q(register_23_q), .clk(cp), .clr(re));
  Register #(.width(32)) register_24 (.D(i0), .en(c32[26]), .Q(register_24_q), .clk(cp), .clr(re));
  Register #(.width(32)) register_25 (.D(i0), .en(c32[1]), .Q(register_25_q), .clk(cp), .clr(re));
  Register #(.width(32)) register_26 (.D(i0), .en(c32[9]), .Q(register_26_q), .clk(cp), .clr(re));
  Register #(.width(32)) register_27 (.D(i0), .en(c32[17]), .Q(register_27_q), .clk(cp), .clr(re));
  Register #(.width(32)) register_28 (.D(i0), .en(c32[25]), .Q(register_28_q), .clk(cp), .clr(re));
  Register #(.width(32)) register_29 (.D(i0), .en(c32[0]), .Q(register_29_q), .clk(cp), .clr(re));
  Register #(.width(32)) register_30 (.D(i0), .en(c32[8]), .Q(register_30_q), .clk(cp), .clr(re));
  Register #(.width(32)) register_31 (.D(i0), .en(c32[16]), .Q(register_31_q), .clk(cp), .clr(re));
  Register #(.width(32)) register_32 (.D(i0), .en(c32[24]), .Q(register_32_q), .clk(cp), .clr(re));
  Multiplexer #(.enable("false"), .select(5), .width(32)) multiplexer_1 (
    .in0(register_29_q), .in1(register_25_q), .in2(register_18_q), .in3(register_17_q), .in4(register_13_q),
    .in5(register_9_q), .in6(register_5_q), .in7(register_1_q), .in8(register_30_q), .in9(register_26_q),
    .in10(register_20_q), .in11(register_19_q), .in12(register_14_q), .in13(register_10_q),
    .in14(register_6_q), .in15(register_2_q), .in16(register_31_q), .in17(register_27_q),
    .in18(register_22_q), .in19(register_21_q), .in20(register_15_q), .in21(register_11_q),
    .in22(register_7_q), .in23(register_3_q), .in24(register_32_q), .in25(register_28_q),
    .in26(register_24_q), .in27(register_23_q), .in28(register_16_q), .in29(register_12_q),
    .in30(register_8_q), .in31(register_4_q), .out(o0), .sel(choose0));
  Multiplexer #(.enable("false"), .select(5), .width(32)) multiplexer_2 (
    .in0(register_29_q), .in1(register_25_q), .in2(register_18_q), .in3(register_17_q), .in4(register_13_q),
    .in5(register_9_q), .in6(register_5_q), .in7(register_1_q), .in8(register_30_q), .in9(register_26_q),
    .in10(register_20_q), .in11(register_19_q), .in12(register_14_q), .in13(register_10_q),
    .in14(register_6_q), .in15(register_2_q), .in16(register_31_q), .in17(register_27_q),
    .in18(register_22_q), .in19(register_21_q), .in20(register_15_q), .in21(register_11_q),
    .in22(register_7_q), .in23(register_3_q), .in24(register_32_q), .in25(register_28_q),
    .in26(register_24_q), .in27(register_23_q), .in28(register_16_q), .in29(register_12_q),
    .in30(register_8_q), .in31(register_4_q), .out(o1), .sel(choose1));
endmodule

module IM (
  input  [29:0] i,
  output [31:0] o
);

  ROM #(.addrWidth(5), .dataWidth(32)) rom_1 (.addr(i[4:0]), .data(o));

  // Notes on the sheet:
  //   contents of rom_1 (hex, n*v repeats v):
  //   228021 228823 34320080 8c330002 ac310002 3c14abcd 10240001 ffffffff 1024ffe0
endmodule

module PC (
  input  cp,
  input  re0,
  input  aaa,
  input  [31:0] sign_ext,
  output [29:0] o
);

  wire button_1_out, or_1_out;
  wire [1:0] undriven;
  wire [29:0] add32_1_sigma;
  wire [31:0] and_1_out;
  wire [31:30] add32_1_sigma_2;

  Button button_1 (.out(button_1_out));
  Register #(.width(30)) register_1 (.D(add32_1_sigma), .en(1'b1), .clk(or_1_out), .Q(o), .clr(re0));
  or or_1 (or_1_out, button_1_out, cp);
  // Probe on add32_1_sigma
  // Probe on and_1_out
  assign and_1_out = {32{aaa}} & {{19{sign_ext[15]}}, sign_ext[14:2]};  // AND_Gate and_1, 32 bits wide
  add32 add32_1 (.c0(1'b1), .a({undriven, o}), .b(and_1_out), .sigma({add32_1_sigma_2, add32_1_sigma}));  // open: c32
endmodule

module mian (
);

  wire clk_out, controller_1_extop, controller_1_memwrite, controller_1_npc_sel, controller_1_regdst,
       controller_1_regwrite, cp_debug_out, not_1_out, or_1_out, or_2_out, or_3_out, reset_out;
  wire [1:0] controller_1_aluop, controller_1_memtoreg;
  wire [3:0] alu_1_c_5, alu_1_c_6, alu_1_c_7;
  wire [4:0] alu_1_c, alu_1_c_2, alu_1_c_3, alu_1_c_4, multiplexer_1_out, multiplexer_1_out_2,
       multiplexer_1_out_3;
  wire [14:0] undriven;
  wire [15:0] ifu_1_instr;
  wire [31:0] dm_1_out_dm, ext_1_b, gpr_1_rd1, gpr_1_rd2, multiplexer_2_out, multiplexer_3_out;
  wire [31:26] ifu_1_instr_2;

  // Probe on multiplexer_1_out
  // Probe on multiplexer_1_out_2
  // Probe on multiplexer_1_out_3
  // Probe on ifu_1_instr
  Multiplexer #(.enable("false"), .width(15)) multiplexer_1 (
    .in0(undriven), .in1({ifu_1_instr[15:11], undriven[14:10], undriven[4:0]}),
    .out({multiplexer_1_out_3, multiplexer_1_out_2, multiplexer_1_out}), .sel(controller_1_regdst));
  // Probe on ifu_1_instr
  or or_1 (or_1_out, 1'b0, reset_out);
  GPR gpr_1 (
    .Wd(multiplexer_3_out), .Regwrite(controller_1_regwrite), .Clk(or_2_out), .Reset(1'b0),
    .A1(multiplexer_1_out), .A2(multiplexer_1_out_2), .A3(multiplexer_1_out_3), .Rd1(gpr_1_rd1),
    .Rd2(gpr_1_rd2));
  // Probe on gpr_1_rd2
  EXT ext_1 (.A(ifu_1_instr), .Extop(controller_1_extop), .B(ext_1_b));
  // Probe on ifu_1_instr[10:6]
  IFU ifu_1 (
    .IfBeq(controller_1_npc_sel), .Zero(or_3_out), .Clk(or_2_out), .Reset(or_1_out),
    .Instr({ifu_1_instr_2, undriven[4:0], undriven[14:10], ifu_1_instr}));
  // Probe on {ifu_1_instr_2, undriven[4:0], undriven[14:10], ifu_1_instr}
  // Probe on gpr_1_rd1
  // Probe on ext_1_b
  Multiplexer #(.enable("false"), .width(32)) multiplexer_2 (
    .in0(gpr_1_rd2), .in1(ext_1_b), .out(multiplexer_2_out), .sel(controller_1_memtoreg[1]));
  // Probe on multiplexer_2_out
  // Probe on controller_1_aluop
  // Probe on ifu_1_instr_2
  // Probe on ifu_1_instr[5:0]
  // Probe on multiplexer_3_out
  Multiplexer #(.enable("false"), .select(2), .width(32)) multiplexer_3 (
    .in0({alu_1_c_7, alu_1_c_6, alu_1_c_5, alu_1_c_4, alu_1_c_3, alu_1_c_2, alu_1_c}), .in1(ext_1_b),
    .in2({alu_1_c_7, alu_1_c_6, alu_1_c_5, alu_1_c_4, alu_1_c_3, alu_1_c_2, alu_1_c}), .in3(dm_1_out_dm),
    .out(multiplexer_3_out));  // open: sel
  ALU alu_1 (
    .F(controller_1_aluop), .A(gpr_1_rd1), .B(multiplexer_2_out),
    .C({alu_1_c_7, alu_1_c_6, alu_1_c_5, alu_1_c_4, alu_1_c_3, alu_1_c_2, alu_1_c}));
  Controller controller_1 (
    .op(ifu_1_instr_2), .func(ifu_1_instr[5:0]), .Regdst(controller_1_regdst),
    .Alusrc(controller_1_memtoreg[1]), .Memtoreg(controller_1_memtoreg[0]), .RegWrite(controller_1_regwrite),
    .Memwrite(controller_1_memwrite), .npc_sel(controller_1_npc_sel), .Extop(controller_1_extop),
    .Aluop(controller_1_aluop));
  // Probe on {alu_1_c_7, alu_1_c_6, alu_1_c_5, alu_1_c_4, alu_1_c_3, alu_1_c_2, alu_1_c}
  not not_1 (not_1_out, controller_1_memwrite);
  or or_2 (or_2_out, clk_out, cp_debug_out);
  // Probe on gpr_1_rd2
  // Probe on alu_1_c
  Clock clk (.out(clk_out));
  Button cp_debug (.out(cp_debug_out));
  Button reset (.out(reset_out));
  or or_3 (or_3_out, 1'b0, alu_1_c_7[3], alu_1_c_7[2], alu_1_c_7[1], alu_1_c_7[0], alu_1_c_6[3], alu_1_c_6[2], alu_1_c_6[1], alu_1_c_6[0], alu_1_c_5[3], alu_1_c_5[2], alu_1_c_5[1], alu_1_c_5[0], alu_1_c_4[4], alu_1_c_4[3], alu_1_c_4[2], alu_1_c_4[1], alu_1_c_4[0], alu_1_c_3[4], alu_1_c_3[3], alu_1_c_3[2], alu_1_c_3[1], alu_1_c_3[0], alu_1_c_2[4], alu_1_c_2[3], alu_1_c_2[2], alu_1_c_2[1], alu_1_c_2[0], alu_1_c[4], alu_1_c[3], alu_1_c[2], alu_1_c[1], alu_1_c[0]);
  DM dm_1 (
    .D(gpr_1_rd2), .Memtoreg(not_1_out), .Memwrite(controller_1_memwrite), .Clk(or_2_out), .Reset(1'b0),
    .A(alu_1_c), .out_DM(dm_1_out_dm));
  // Probe on dm_1_out_dm
endmodule

module Controller (
  input  [5:0] op,
  input  [5:0] func,
  output Regdst,
  output Alusrc,
  output Memtoreg,
  output RegWrite,
  output Memwrite,
  output npc_sel,
  output Extop,
  output [1:0] Aluop
);

  wire not_1_out, not_2_out, not_3_out, not_4_out, not_5_out, not_6_out, not_7_out, not_8_out, not_9_out,
       not_10_out, not_11_out, not_12_out;
  wire [6:0] LUI_out;

  not not_1 (not_1_out, func[0]);
  not not_2 (not_2_out, func[1]);
  not not_3 (not_3_out, func[2]);
  not not_4 (not_4_out, func[3]);
  not not_5 (not_5_out, func[4]);
  not not_6 (not_6_out, func[5]);
  not not_7 (not_7_out, op[0]);
  not not_8 (not_8_out, op[1]);
  not not_9 (not_9_out, op[2]);
  not not_10 (not_10_out, op[3]);
  not not_11 (not_11_out, op[4]);
  not not_12 (not_12_out, op[5]);
  and ADDU (LUI_out[6], func[5], not_5_out, not_4_out, not_3_out, not_2_out, func[0], not_12_out, not_11_out, not_10_out, not_9_out, not_8_out, not_7_out);
  or or_1 (Regdst, LUI_out[6], LUI_out[5], Memwrite);
  or or_2 (Alusrc, LUI_out[4], LUI_out[3], Memwrite);
  or or_3 (Memtoreg, LUI_out[3], LUI_out[0]);
  or or_4 (RegWrite, LUI_out[6], LUI_out[5], LUI_out[4], LUI_out[3], LUI_out[0]);
  or or_5 (Extop, Memwrite, LUI_out[0]);
  or or_6 (Aluop[0], LUI_out[6], LUI_out[4], LUI_out[3], Memwrite);
  or or_7 (Aluop[1], LUI_out[6], LUI_out[5], LUI_out[3], Memwrite, npc_sel);
  and SUBU (LUI_out[5], func[5], not_5_out, not_4_out, not_3_out, func[1], func[0], not_12_out, not_11_out, not_10_out, not_9_out, not_8_out, not_7_out);
  and ORI (LUI_out[4], not_12_out, not_11_out, op[3], op[2], not_8_out, op[0]);
  and LW (LUI_out[3], op[5], not_11_out, not_10_out, not_9_out, op[1], op[0]);
  and SW (Memwrite, op[5], not_11_out, op[3], not_9_out, op[1], op[0]);
  and BEQ (npc_sel, not_12_out, not_11_out, not_10_out, op[2], not_8_out, not_7_out);
  and LUI (LUI_out[0], not_12_out, not_11_out, op[3], op[2], op[1], op[0]);
endmodule

module IFU (
  input  IfBeq,
  input  Zero,
  input  Clk,
  input  Reset,
  output [31:0] Instr
);

  wire and_1_out;
  wire [29:0] pc_1_o;

  and and_1 (and_1_out, IfBeq, Zero);
  PC pc_1 (.cp(Clk), .re0(Reset), .aaa(and_1_out), .sign_ext(Instr), .o(pc_1_o));
  IM im_1 (.i(pc_1_o), .o(Instr));
endmodule

module GPR (
  input  [31:0] Wd,
  input  Regwrite,
  input  Clk,
  input  Reset,
  input  [4:0] A1,
  input  [4:0] A2,
  input  [4:0] A3,
  output [31:0] Rd1,
  output [31:0] Rd2
);

  wire button_1_out, not_1_out, or_1_out, or_2_out;
  wire [31:0] decoder_1_out0, register_1_q, register_2_q;

  Button button_1 (.out(button_1_out));
  or or_1 (or_1_out, button_1_out, Clk);
  Decoder #(.select(5)) decoder_1 (
    .out0(decoder_1_out0[0]), .out1(decoder_1_out0[1]), .out2(decoder_1_out0[2]), .out3(decoder_1_out0[3]),
    .out4(decoder_1_out0[4]), .out5(decoder_1_out0[5]), .out6(decoder_1_out0[6]), .out7(decoder_1_out0[7]),
    .out8(decoder_1_out0[8]), .out9(decoder_1_out0[9]), .out10(decoder_1_out0[10]),
    .out11(decoder_1_out0[11]), .out12(decoder_1_out0[12]), .out13(decoder_1_out0[13]),
    .out14(decoder_1_out0[14]), .out15(decoder_1_out0[15]), .out16(decoder_1_out0[16]),
    .out17(decoder_1_out0[17]), .out18(decoder_1_out0[18]), .out19(decoder_1_out0[19]),
    .out20(decoder_1_out0[20]), .out21(decoder_1_out0[21]), .out22(decoder_1_out0[22]),
    .out23(decoder_1_out0[23]), .out24(decoder_1_out0[24]), .out25(decoder_1_out0[25]),
    .out26(decoder_1_out0[26]), .out27(decoder_1_out0[27]), .out28(decoder_1_out0[28]),
    .out29(decoder_1_out0[29]), .out30(decoder_1_out0[30]), .out31(decoder_1_out0[31]), .sel(A3),
    .en(Regwrite));
  not not_1 (not_1_out, Regwrite);
  reg32 reg32_1 (
    .choose0(A1), .choose1(A2), .cp(or_1_out), .i0(Wd), .re(Reset), .c32(decoder_1_out0), .o0(Rd1), .o1(Rd2));
  // Probe on register_1_q
  or or_2 (or_2_out, 1'b1, not_1_out);
  Register #(.width(32)) register_1 (.D(Rd1), .en(or_2_out), .Q(register_1_q), .clk(or_1_out), .clr(Reset));
  // Probe on register_2_q
  Register #(.width(32)) register_2 (.D(Rd2), .en(or_2_out), .Q(register_2_q), .clk(or_1_out), .clr(Reset));
endmodule

module ALU (
  input  [1:0] F,
  input  [31:0] A,
  input  [31:0] B,
  output [31:0] C
);

  wire and_1_out, not_1_out;
  wire [31:0] add32_1_sigma, and_2_out, multiplexer_1_out, multiplexer_2_out, not_2_out, or_1_out;

  // Probe on A
  // Probe on B
  // Probe on C
  not not_1 (not_1_out, F[0]);
  and and_1 (and_1_out, F[1], not_1_out);
  assign not_2_out = ~B;  // NOT_Gate not_2, 32 bits wide
  Multiplexer #(.enable("false"), .width(32)) multiplexer_1 (
    .in0(B), .in1(not_2_out), .out(multiplexer_1_out), .sel(and_1_out));
  assign and_2_out = B & A;  // AND_Gate and_2, 32 bits wide
  assign or_1_out = B | A;  // OR_Gate or_1, 32 bits wide
  add32 add32_1 (.c0(and_1_out), .a(A), .b(multiplexer_1_out), .sigma(add32_1_sigma));  // open: c32
  Multiplexer #(.enable("false"), .width(32)) multiplexer_2 (
    .in0(and_2_out), .in1(or_1_out), .out(multiplexer_2_out), .sel(F[0]));
  Multiplexer #(.enable("false"), .width(32)) multiplexer_3 (
    .in0(multiplexer_2_out), .in1(add32_1_sigma), .out(C), .sel(F[1]));
endmodule

module DM (
  input  [31:0] D,
  input  Memtoreg,
  input  Memwrite,
  input  Clk,
  input  Reset,
  input  [4:0] A,
  output [31:0] out_DM
);

  RAM #(.addrWidth(5), .clearpin("true"), .dataWidth(32), .readbehav("war")) ram_1 (
    .addr(A), .we(Memwrite), .oe(Memtoreg), .clk(Clk), .din(D), .dout(out_DM), .clr(Reset));
endmodule

module EXT (
  input  [15:0] A,
  input  Extop,
  output [31:0] B
);

  Multiplexer #(.enable("false"), .width(32)) multiplexer_1 (
    .in0({{16{1'b0}}, A}), .in1({A, {16{1'b0}}}), .out(B), .sel(Extop));
endmodule
